# Fritzing sketch single_traffic_light (saved by Fritzing 0.8.7b)
breadboards: 1

parts:
  Part1 = Arduino Uno (Rev3)
  LED6 = LED - 5mm [color="Red (633nm)" package="5 mm [THT]"]
  R7 = Resistor [tolerance=±5% resistance=330 package=THT]
  LED5 = LED - 5mm [color="Yellow (585nm)" package="5 mm [THT]"]
  R9 = Resistor [tolerance=±5% resistance=330 package=THT]
  LED4 = LED - 5mm [color="Green (555nm)" package="5 mm [THT]"]
  R8 = Resistor [tolerance=±5% resistance=330 package=THT]

nets:
  N1: Part1.GND, R7.Pin_0, R9.Pin_0, R8.Pin_0
  N2: Part1.D4, LED4.anode
  N3: Part1.D5_PWM, LED5.anode
  N4: Part1.D6_PWM, LED6.anode
  N5: LED6.cathode, R9.Pin_1
  N6: R7.Pin_1, LED4.cathode
  N7: LED5.cathode, R8.Pin_1
